# Fritzing sketch Cylon-leap-4servos (saved by Fritzing 0.9.2b)
breadboards: 1

parts:
  Part1 = Arduino Uno (Rev3)
  Power_plug1 = Power plug
  J1 = Basic Servo
  J2 = Basic Servo
  J3 = Basic Servo
  J4 = Basic Servo

nets:
  N1: Part1.D9_PWM, J2.pulse
  N2: Part1.D10_PWM/SS, J1.pulse
  GND: Part1.GND, Power_plug1.GND, J1.gnd, J2.gnd, J3.gnd, J4.gnd
  N3: Part1.D5_PWM, J4.pulse
  VCC: Power_plug1.VCC, J1.vcc, J2.vcc, J3.vcc, J4.vcc

notes:
  PWM 5 - Pan
  PWM 6 - Tilt
  PWM 9 - Pan
  PWM 10 - Tilt
  Separate power supply to breadboard for servos: 5v, 2a
  Four micro servos, each pair mounted in pan-tilt kits
  USB cable in from computer, powering Arduino and running CylonJS/Firmata connecting LeapMotion
